// Logisim project Full Adder.circ as structural Verilog: 1 circuit, main circuit main
module main (
  input  A,
  input  B,
  input  C,
  output SUM,
  output CARRY
);

  wire and_1_out, and_2_out, xor_1_out;

  xor xor_1 (xor_1_out, A, B);
  and and_1 (and_1_out, xor_1_out, C);
  xor xor_2 (SUM, xor_1_out, C);
  and and_2 (and_2_out, A, B);
  or or_1 (CARRY, and_2_out, and_1_out);
endmodule
